// Logisim project alu-harness.circ as structural Verilog: 1 circuit, main circuit main
module main (
  output [7:0] out_1,
  output [31:0] out_2,
  output out_3,
  output out_4,
  output out_5,
  output halt
);

  wire clock_1_out;
  wire [3:0] Op;
  wire [7:0] adder_1_out;
  wire [31:0] A, B;

  Register register_1 (.D(adder_1_out), .Q(out_1), .clk(clock_1_out));  // open: en, clr
  Clock clock_1 (.out(clock_1_out));
  Comparator #(.mode("unsigned")) comparator_1 (.a({8{1'b1}}), .b(out_1), .eq(halt));  // open: gt, lt
  Adder adder_1 (.a(8'h1), .b(out_1), .out(adder_1_out));  // open: cin, cout
  ROM #(.dataWidth(32)) rom_1 (.addr(out_1), .data(A), .sel(1'b1));
  ROM #(.dataWidth(32)) rom_2 (.addr(out_1), .data(B), .sel(1'b1));
  ROM #(.dataWidth(4)) rom_3 (.addr(out_1), .data(Op), .sel(1'b1));
  ALU alu_1 (.A(A), .B(B), .ALU_Op(Op), .Out(out_2), .Equal(out_3), .LT(out_4), .LTU(out_5));

  // Other names for the same wires on the sheet: _0[31:0] = out_2; _1 = out_3; _2 = out_4; _3 = out_5;
  //   In[7:0] = out_1

  // Notes on the sheet:
  //   Counter
  //   Halt signal
  //   There should be no red/blue wires and the outputs should not be x's
endmodule
