// Logisim project alu.circ as structural Verilog: 1 circuit, main circuit ALU
module ALU (
  input  [31:0] A,
  input  [31:0] B,
  input  [3:0] ALU_Op,
  output [31:0] Out,
  output Equal,
  output LT,
  output LTU
);

  wire carry;
  wire [31:0] add, \and , div_0, mul, mulh, \or , rem, sll, slt, srl, sub, \xor ;

  Multiplexer #(.select(4), .width(32)) multiplexer_1 (
    .in0(sll), .in1(srl), .in2(add), .in3(\and ), .in4(\or ), .in5(\xor ), .in6(slt), .in7(mul), .in8(mulh),
    .in9(div_0), .in10(rem), .in11(sub), .out(Out), .sel(ALU_Op));  // open: in12, in13, in14, in15, en
  Shifter #(.width(32), .shift("lr")) shifter_1 (.in(A), .\dist (B[4:0]), .out(srl));
  Adder #(.width(32)) adder_1 (.a(A), .b(B), .out(add), .cout(carry));  // open: cin
  assign \and  = A & B;  // AND_Gate and_1, 32 bits wide
  assign \or  = A | B;  // OR_Gate or_1, 32 bits wide
  assign \xor  = A ^ B;  // XOR_Gate xor_1, 32 bits wide
  Shifter #(.width(32)) shifter_2 (.in(A), .\dist (B[4:0]), .out(sll));
  Comparator #(.width(32)) comparator_1 (.a(A), .b(B), .eq(Equal), .lt(LT));  // open: gt
  assign slt = {{31{1'b0}}, LT};  // Bit_Extender bit_extender_1
  Multiplier #(.width(32)) multiplier_1 (.a(A), .b(B), .out(mul));  // open: cin, cout
  Multiplier #(.width(32)) multiplier_2 (.a(A), .b(B), .cout(mulh));  // open: out, cin
  Divider #(.width(32)) divider_1 (.a(A), .b(B), .out(div_0), .rem(rem));  // open: upper
  Subtractor #(.width(32)) subtractor_1 (.a(A), .b(B), .out(sub));  // open: bin, bout
  Comparator #(.width(32), .mode("unsigned")) comparator_2 (.a(A), .b(B), .lt(LTU));  // open: gt, eq

  // Other names for the same wires on the sheet: Op[3:0] = ALU_Op

  // Notes on the sheet:
  //   Inputs
  //   NOTE
  //   Please do not modify/replace/move/change/delete/etc input and output pins
  //   Outputs
endmodule
