// Logisim project cpu.circ as structural Verilog: 1 circuit, main circuit CPU
module CPU (
  input  [31:0] Instruction,
  input  CLK,
  output [31:0] s0,
  output [31:0] s1,
  output [31:0] t0,
  output [31:0] t1,
  output [31:0] a0,
  output [31:0] ra,
  output [31:0] sp,
  output [31:0] PC
);

  wire and_1_out, b_type, comparator_1_eq, comparator_2_eq, EQUAL, i_type, j_type, ja_type, jalr_type,
       load_type, LT, LTU, lu_type, or_2_out, or_5_out, PC_op, r_type, rb_type, s_type, u_type, we;
  wire [0:0] or_1_out;
  wire [3:0] op;
  wire [4:0] ALU_select;
  wire [7:0] size8;
  wire [15:8] size16;
  wire [31:0] adder_1_out, ALUOut, bit_extender_5_out, bit_extender_6_out, data, imm, imm_b, imm_i, imm_j,
       imm_s, mem_out, multiplexer_2_out, multiplexer_3_out, pc_4, regfile_1_r1, regfile_1_r2;
  wire [31:16] size32;

  and and_1 (and_1_out, PC_op, b_type);
  Decoder #(.select(5)) decoder_1 (
    .out0(load_type), .out4(i_type), .out8(s_type), .out12(r_type), .out13(u_type), .out24(b_type),
    .out25(jalr_type), .out27(j_type), .sel(Instruction[6:2]));  // open: out1, out2, out3, out5, out6, out7, out9, out10, out11, out14, out15, out16, out17, out18, out19, out20, out21, out22, out23, out26, out28, out29, out30, out31, en
  // Incrementer incrementer_1: pin names not known; wires that end beside it: PC, pc_4
  Adder #(.width(32)) adder_1 (.a(PC), .b(imm), .out(adder_1_out));  // open: cin, cout
  Multiplexer #(.select(3)) multiplexer_1 (
    .in0(EQUAL), .in1(1'b0), .in2(1'b0), .in3(1'b0), .in4(LT), .in5(1'b0), .in6(LTU), .in7(1'b0),
    .out(PC_op), .sel(Instruction[14:12]));  // open: en
  Multiplexer #(.select(2), .width(32)) multiplexer_2 (
    .in0(pc_4), .in1(adder_1_out), .in2(ALUOut), .out(multiplexer_2_out), .sel({jalr_type, or_1_out[0]}));  // open: in3, en
  or or_1 (or_1_out[0], and_1_out, j_type);
  PC pc_1 (.Input(multiplexer_2_out), .Clk(CLK), .Output(PC));
  or or_2 (or_2_out, r_type, b_type);
  or or_3 (lu_type, load_type, u_type);
  or or_4 (ja_type, j_type, u_type, jalr_type);
  assign imm_i = {{20{Instruction[31]}}, Instruction[31:20]};  // Bit_Extender bit_extender_1
  Comparator #(.width(5)) comparator_1 (.a(Instruction[6:2]), .b(5'b01000), .eq(comparator_1_eq));  // open: gt, lt
  Comparator #(.width(5)) comparator_2 (.a(Instruction[6:2]), .b(5'b11000), .eq(comparator_2_eq));  // open: gt, lt
  not not_1 (rb_type, or_2_out);
  RegFile regfile_1 (
    .Clk(CLK), .R1(regfile_1_r1), .R2(regfile_1_r2), .WE(we), .W(data), .RD(Instruction[11:7]),
    .RS1(Instruction[19:15]), .RS2(Instruction[24:20]), .s0(s0), .s1(s1), .t0(t0), .t1(t1), .a0(a0), .ra(ra),
    .sp(sp));
  nor nor_1 (we, comparator_1_eq, comparator_2_eq);
  assign imm_s = {{20{Instruction[31]}}, {Instruction[31:25], Instruction[11:7]}};  // Bit_Extender bit_extender_2
  Multiplexer #(.width(32)) multiplexer_3 (
    .in0(regfile_1_r2), .in1(imm), .out(multiplexer_3_out), .sel(rb_type));  // open: en
  assign imm_b = {{19{Instruction[31]}}, {Instruction[31], Instruction[7], Instruction[30:25], Instruction[11:8], 1'b0}};  // Bit_Extender bit_extender_3
  ALU alu_1 (.A(regfile_1_r1), .B(multiplexer_3_out), .ALU_Op(op), .Out(ALUOut), .Equal(EQUAL), .LT(LT), .LTU(LTU));
  assign imm_j = {{11{Instruction[31]}}, {Instruction[31], Instruction[19:12], Instruction[20], Instruction[30:21], 1'b0}};  // Bit_Extender bit_extender_4
  and and_2 (ALU_select[3], Instruction[25], r_type);
  Multiplexer #(.select(2), .width(32)) multiplexer_4 (
    .in0(ALUOut), .in1(mem_out), .in2(pc_4), .in3({Instruction[31:12], {12{1'b0}}}), .out(data),
    .sel({ja_type, lu_type}));  // open: en
  memory_main main_1 (.Address(ALUOut), .WE(s_type), .Data(regfile_1_r2), .Out({size32, size16, size8}), .Clk(CLK));
  Multiplexer #(.select(5), .width(4)) multiplexer_5 (
    .in0(4'b0010), .in1(4'b0000), .in2(4'b0110), .in4(4'b0101), .in5(4'b0001), .in6(4'b0100), .in7(4'b0011),
    .in8(4'b0111), .in9(4'b1000), .in12(4'b1001), .in14(4'b1010), .in16(4'b1011), .out(op), .sel(ALU_select));  // open: in3, in10, in11, in13, in15, in17, in18, in19, in20, in21, in22, in23, in24, in25, in26, in27, in28, in29, in30, in31, en
  Multiplexer #(.select(5), .width(32)) multiplexer_6 (
    .in0(imm_i), .in4(imm_i), .in8(imm_s), .in13({Instruction[31:12], {12{1'b0}}}), .in24(imm_b),
    .in25(imm_i), .in27(imm_j), .out(imm), .sel(Instruction[6:2]));  // open: in1, in2, in3, in5, in6, in7, in9, in10, in11, in12, in14, in15, in16, in17, in18, in19, in20, in21, in22, in23, in26, in28, in29, in30, in31, en
  or or_5 (or_5_out, i_type, r_type);
  and and_3 (ALU_select[4], Instruction[30], r_type);
  Multiplexer #(.width(3)) multiplexer_7 (
    .in0(3'b000), .in1(Instruction[14:12]), .out(ALU_select[2:0]), .sel(or_5_out));  // open: en
  assign bit_extender_5_out = {{24{size8[7]}}, size8};  // Bit_Extender bit_extender_5
  assign bit_extender_6_out = {{16{size16[15]}}, {size16, size8}};  // Bit_Extender bit_extender_6
  Multiplexer #(.select(2), .width(32)) multiplexer_8 (
    .in0(bit_extender_5_out), .in1(bit_extender_6_out), .in2({size32, size16, size8}), .out(mem_out),
    .sel(Instruction[13:12]));  // open: in3, en

  // Other names for the same wires on the sheet: b_imm7_11[4:0] = Instruction[11:7]; INST[31:0] = Instruction;
  //   rd[4:0] = Instruction[11:7]; s_imm0_4[4:0] = Instruction[11:7]; fetch_addr[31:0] = PC;
  //   func3[2:0] = Instruction[14:12]; imm_u[31:12] = Instruction[31:12]; j_imm12_19[7:0] = Instruction[19:12];
  //   j_imm12_31[19:0] = Instruction[31:12]; u_imm12_31[19:0] = Instruction[31:12]; rs1[4:0] = Instruction[19:15];
  //   j_imm11 = Instruction[20]; rs2[4:0] = Instruction[24:20]; j_imm1_10[9:0] = Instruction[30:21];
  //   b_imm25_31[6:0] = Instruction[31:25]; func7[6:0] = Instruction[31:25]; s_imm5_11[6:0] = Instruction[31:25];
  //   j_imm20 = Instruction[31]; opcode[4:0] = Instruction[6:2]; size16[7:0] = size8; size32[15:0] = {size16, size8};
  //   write_type[1:0] = {ja_type, lu_type}

  // Notes on the sheet:
  //   3: bits 7-11 rd
  //   4: bits 15-19 rs1
  //   5: bits 20-23 rs2
  //   jtype
  //   FLAGS salen del regfile
  //   0 (top) bits 2-6: opcode
  //   1: bits 12-14 func3
  //   2: bits 25-31 func7
  //   NOTE
  //   Please do not modify/replace/move/change/delete/etc input and output pins
  //   rtype
  //   itype
  //   stype
  //   btype
  //   utype
  //   Stype y Btype WE=false, de lo contrario True
  //   Etos 4 campos vienen del CU
  //   UNIDAD DE CONTROL
  //   I: 00100XX: 4
  //   S: 01000xx: 8 
  //   R: 01100XX: 12
  //   U:01101xx:13
  //   B: 11000xx: 24
  //   J:11011xx:27
  //   These are debug/test outputs from your circuit
  //   Basiamente Func3 es solo relevante par a itype y rtype
  //   func7[0] AND r_type
  //   Aca deberia calcular un valor de opcode/func3/func7 para mandar un op al ALU.
  //   func7[5] AND r_type
  //   Señal de control elegida, va a ALU
  //   Señal de control elegida, va a ALU
endmodule
