// Logisim project memory.circ as structural Verilog: 1 circuit, main circuit main
module main (
  input  [31:0] Address,
  input  WE,
  input  Clk,
  input  [31:0] Data,
  output [31:0] Out
);

  wire [23:0] bit_extender_1_out;

  Bit_Extender #(.in_width(32), .out_width(24)) bit_extender_1 (.in(Address), .out(bit_extender_1_out));
  RAM #(.addrWidth(24), .dataWidth(32), .bus("separate")) ram_1 (
    .addr(bit_extender_1_out), .din(Data), .data(Out), .str(WE), .sel(1'b1), .clk(Clk), .ld(1'b1), .clr(1'b0));
endmodule
