// Logisim project pc.circ as structural Verilog: 1 circuit, main circuit PC
module PC (
  input  [31:0] Input,
  input  Enable,
  input  Clk,
  input  Reset,
  output [31:0] Output
);

  Register #(.width(32)) PC (.D(Input), .en(Enable), .Q(Output), .clk(Clk), .clr(Reset));
endmodule
