// Logisim project riscv.circ as structural Verilog: 1 circuit, main circuit RISC-V
module RISC_V (
  output [31:0] s0,
  output [31:0] s1,
  output [31:0] t0,
  output [31:0] t1,
  output [31:0] a0,
  output [31:0] ra,
  output [31:0] sp,
  output [15:0] Time_Step,
  output [31:0] out_9,
  output [31:0] out_10
);

  wire clk;

  Counter #(.width(16), .max('hffff)) counter_1 (.Q(Time_Step), .clk(clk));  // open: load, D, count, carry, clr
  CPU cpu_1 (
    .CLK(clk), .Instruction(out_10), .PC(out_9), .s0(s0), .s1(s1), .t0(t0), .t1(t1), .a0(a0), .ra(ra), .sp(sp));
  Clock clock_1 (.out(clk));
  // Probe on out_9
  // RISC_VProgramROM risc_vprogramrom_1: pin names not known; wires that end beside it: out_9, out_10
  // Probe on out_10

  // Other names for the same wires on the sheet: fetch_addr[31:0] = out_9; instruction[31:0] = out_10

  // Notes on the sheet:
  //   These are debug/test outputs from your circuit
endmodule
